# Fritzing sketch blinkm_ftdi (saved by Fritzing 0.9.4)
breadboards: 1

parts:
  Part2 = BlinkM
  R1 = Resistor [tolerance=±5% resistance=220 package="2512 [SMD]"]
  R2 = Resistor [tolerance=±5% resistance=220 package="2512 [SMD]"]
  J2 = double row male pin header, 14 pins [form="♂ (male)"]
  J3 = double row male pin header, 14 pins [form="♂ (male)"]
  J4 = double row male pin header, 14 pins [form="♂ (male)"]
  J5 = double row male pin header, 14 pins [form="♂ (male)"]

nets:
  N1: Part2.SDA, R2.Pin_0, J2.pin5, J4.pin5
  N2: Part2.SCL, R1.Pin_0, J2.pin4
  N3: Part2.GND, J4.pin1
  N4: Part2.VCC, R1.Pin_1, R2.Pin_1, J3.pin1, J3.pin2
  N5: J2.pin1, J2.pin2, J2.pin3, J2.pin7, J2.pin12, J5.pin7, J5.pin12

notes:
  CN2
  FT4232H
  CN3
  CN2-1
  CN3-1
  SCL
  SDA
  4.7kOhm Pullup Resistors
  USB 5V VCC Out
  VCC In

custom parts:
  BlinkM: BlinkM component
